# Fritzing sketch wirelessWatchdogVeroLayoutV18 (saved by Fritzing 0.9.3b)
stripboards: 1

parts:
  Part1 = Arduino Nano (Rev3.0)
  Part2 = NRF24L01+ Breakout Board  # not connected
  433Tx1 = 433Mhz Transmitter - 3 pins [form="♂ (male)" package=THT]
  433Mhz_Rx2 = 433Mhz Receiver - 4 pins [form="♂ (male)" package=THT]
  J1 = Piezo Speaker  # not connected
  LED2 = LED - 5mm [color="Red (633nm)" package="5 mm [THT]"]
  LED3 = LED - 5mm [color="Green (555nm)" package="5 mm [THT]"]
  R1 = Resistor [tolerance=±5% resistance=470 package=THT]
  Grove1 = Grove OLED 128x96  # not connected
  LED4 = LED - 5mm [color="Blue (470nm)" package="5 mm [THT]"]
  nrfL24L01+1 = nrf24l01+ [form="♂ (male)" package=THT]
  R3 = Resistor [tolerance=±5% resistance=470 package=THT]
  R4 = Resistor [tolerance=±5% resistance=470 package=THT]
  Analogue_Keys1 = Analogue_Keys [form="♂ (male)" package=THT]
  OLED_serial_header1 = OLED serial header [form="♂ (male)" package=THT]
  R5 = Resistor [tolerance=±5% resistance=10k package=THT]
  switch = male pin header, 2 pins [form="♂ (male)"]

nets:
  GND: Part1.RESET, Part1.GND, 433Tx1.GND, 433Mhz_Rx2.GND, LED2.cathode, LED3.cathode, LED4.cathode, nrfL24L01+1.GND, Analogue_Keys1.GND, OLED_serial_header1.GND, switch.pin1
  N1: Part1.D2, 433Mhz_Rx2.DataRx1
  N2: Part1.D3, R1.Pin_1
  N3: Part1.D5, 433Tx1.data
  N4: Part1.D7, nrfL24L01+1.CE
  N5: Part1.D8, nrfL24L01+1.CSN
  N6: Part1.D9, R3.Pin_1
  N7: Part1.D10, R4.Pin_1
  N8: Part1.D11/MOSI, nrfL24L01+1.MOSI
  N9: Part1.D12/MISO, nrfL24L01+1.MISO
  VCC: Part1.5V, 433Tx1.Vcc, 433Mhz_Rx2.Vcc, nrfL24L01+1.+5V, Analogue_Keys1.Vcc, OLED_serial_header1.Vcc, R5.Pin_0
  N10: Part1.A7, R5.Pin_1, switch.pin2
  N11: Part1.A5, OLED_serial_header1.SDA
  N12: Part1.A4, OLED_serial_header1.SCL
  N13: Part1.A0, Analogue_Keys1.Out
  N14: Part1.D13/SCK, nrfL24L01+1.SCK
  N15: LED2.anode, R1.Pin_0
  N16: LED3.anode, R4.Pin_0
  N17: LED4.anode, R3.Pin_0

notes:
  add switch if
  add asbasp icsp header
  add switch for option select
  add buttons if
  NewRemoteTransmitter transmitter(282830, 5, 254, 4);
  nRF24L01 radio on SPI bus plus pins 7 & 8
  RF24 radio(7, 8);
  Tx433Mhz_pin = 5;
  Rx433Mhz_pin = 2;
  redLEDPin = D3;
  greenLEDPin = 10;
  blueLEDPin = 9
  buzzer = 6;
  switchPin = 9;

custom parts:
  433Mhz Transmitter - 3 pins: 433Mhz Transmitter
  nrf24l01+: Generic male header
  Analogue_Keys: Generic male header
  OLED serial header: Generic male header
